# Fritzing sketch ApproxyClock (saved by Fritzing 0.8.7b)
circuit board: 5cm x 3cm
circuit board: 5cm x 3cm
circuit board: 5cm x 2cm
breadboards: 5

parts:
  VCC1 = 4 x AAA Battery Mount
  A1 = atmega328 [package=dip]
  C2 = Capacitor [package=cap-pth-small2]
  C1 = Capacitor [package=cap-pth-small2]
  Y1 = CRYSTAL [package=crystal-smd-10.5x4.8-2pin]
  LED1 = RGB LED (com. cathode, rbg) [package="5 mm [THT]"]
  LED2 = RGB LED (com. cathode, rbg) [package="5 mm [THT]"]
  R1_R = Resistor [tolerance=±5% resistance=1k package=THT]
  R1_B = Resistor [tolerance=±5% resistance=1k package=THT]
  R1_G = Resistor [tolerance=±5% resistance=1k package=THT]
  R2_R = Resistor [tolerance=±5% resistance=1k package=THT]
  R2_G = Resistor [tolerance=±5% resistance=1k package=THT]
  R2_B = Resistor [tolerance=±5% resistance=1k package=THT]
  RT2S1 = Resistor [tolerance=±5% resistance=1k package=THT]
  RT1S1 = Resistor [tolerance=±5% resistance=1k package=THT]
  RT1H1 = Resistor [tolerance=±5% resistance=1M package=THT]
  TR1 = Resistor [tolerance=±5% resistance=0 package=THT]
  TL1 = Resistor [tolerance=±5% resistance=0 package=THT]
  RT2H1 = Resistor [tolerance=±5% resistance=1M package=THT]
  JP = female pin header, 2 pins [form="♀ (female)"]
  JT = female pin header, 3 pins [form="♀ (female)"]
  JL = female pin header, 7 pins [form="♀ (female)"]
  JLM = female pin header, 7 pins [form="♀ (female)"]
  JSM = female pin header, 3 pins [form="♀ (female)"]

nets:
  N1: VCC1.-, A1.GND, C2.2, C1.2, LED1.common_cathode, LED2.common_cathode, JP.pin1, JL.pin7, JLM.pin7
  N2: VCC1.+, A1.VCC, A1.AVCC, A1.AREF, JP.pin2
  N3: A1.D2, RT1S1.Pin_1, RT1H1.Pin_0, JT.pin1, JSM.pin1
  N4: A1.D3_(PWM), R1_B.Pin_0, JL.pin2, JLM.pin2
  N5: A1.D4, RT1H1.Pin_1, RT2H1.Pin_0, JT.pin3, JSM.pin3
  N6: A1.XLAT1, C1.1, Y1.1
  N7: A1.XLAT2, C2.1, Y1.2
  N8: A1.D5_(PWM), R1_R.Pin_0, JL.pin1, JLM.pin1
  N9: A1.D6_(PWM), R1_G.Pin_0, JL.pin3, JLM.pin3
  N10: A1.D7, RT2S1.Pin_1, RT2H1.Pin_1, JT.pin2, JSM.pin2
  N11: A1.D9_(PWM), R2_B.Pin_0, JL.pin5, JLM.pin5
  N12: A1.D10_(PWM), R2_R.Pin_0, JL.pin4, JLM.pin4
  N13: A1.D11_(PWM), R2_G.Pin_0, JL.pin6, JLM.pin6
  N14: LED1.red_anode, R1_R.Pin_1
  N15: LED1.blue_anode, R1_B.Pin_1
  N16: LED1.green_anode, R1_G.Pin_1
  N17: LED2.red_anode, R2_R.Pin_1
  N18: LED2.blue_anode, R2_B.Pin_1
  N19: LED2.green_anode, R2_G.Pin_1
  N20: RT2S1.Pin_0, TR1.Pin_0
  N21: RT1S1.Pin_0, TL1.Pin_1

notes:
  Capacitors: 22 pF
  Crystal: 16 MHz
  Followed the same wiring as the RGB LED supplied by Fritzing, which is not the RGB LED I use
