# Fritzing sketch approxyclock (saved by Fritzing 0.9.6b)
circuit board: 5cm x 10cm
breadboards: 2

parts:
  VCC1 = 4 x AAA Battery Mount
  A1 = atmega328 [package=dip]
  C2 = Capacitor [package=cap-pth-small2]
  C1 = Capacitor [package=cap-pth-small2]
  Y1 = CRYSTAL [package=crystal-smd-10.5x4.8-2pin]
  LED1 = RGB LED (com. cathode, rbg) [package="5 mm [THT]"]
  LED2 = RGB LED (com. cathode, rbg) [package="5 mm [THT]"]
  R1 = Resistor [tolerance=±5% resistance=1k power=0.25 package=THT]
  R2 = Resistor [tolerance=±5% resistance=1k power=0.25 package=THT]
  R3 = Resistor [tolerance=±5% resistance=1k power=0.25 package=THT]
  R4 = Resistor [tolerance=±5% resistance=1k power=0.25 package=THT]
  R5 = Resistor [tolerance=±5% resistance=1k power=0.25 package=THT]
  R6 = Resistor [tolerance=±5% resistance=1k power=0.25 package=THT]
  RHR = Resistor [tolerance=±5% resistance=1k power=0.25 package=THT]
  RHL = Resistor [tolerance=±5% resistance=1k power=0.25 package=THT]
  RSL = Resistor [tolerance=±5% resistance=1M power=0.25 package=THT]
  RTR = Resistor [tolerance=±5% resistance=0 power=0.25 package=THT]
  RTL = Resistor [tolerance=±5% resistance=0 power=0.25 package=THT]
  RSR = Resistor [tolerance=±5% resistance=1M power=0.25 package=THT]
  J1 = female pin header, 2 pins [form="♀ (female)"]
  D1 = Rectifier Diode [part_number=1N4001 package="300 mil [THT]"]

nets:
  N1: VCC1.-, A1.GND, C2.2, C1.2, LED1.common_cathode, LED2.common_cathode, J1.pin2
  N2: VCC1.+, J1.pin1, D1.anode
  N3: A1.D2, RHL.Pin_1
  N4: A1.D3_(PWM), R2.Pin_0
  N5: A1.D4, RSL.Pin_1, RSR.Pin_0
  N6: A1.VCC, A1.AVCC, A1.AREF, D1.cathode
  N7: A1.XLAT1, C1.1, Y1.1
  N8: A1.XLAT2, C2.1, Y1.2
  N9: A1.D5_(PWM), R1.Pin_0
  N10: A1.D6_(PWM), R3.Pin_0
  N11: A1.D7, RHR.Pin_0
  N12: A1.D9_(PWM), R6.Pin_0
  N13: A1.D10_(PWM), R4.Pin_0
  N14: A1.D11_(PWM), R5.Pin_0
  N15: LED1.red_anode, R1.Pin_1
  N16: LED1.blue_anode, R2.Pin_1
  N17: LED1.green_anode, R3.Pin_1
  N18: LED2.red_anode, R4.Pin_1
  N19: LED2.blue_anode, R6.Pin_1
  N20: LED2.green_anode, R5.Pin_1
  N21: RHR.Pin_1, RTR.Pin_1, RSR.Pin_1
  N22: RHL.Pin_0, RSL.Pin_0, RTL.Pin_1

notes:
  Capacitors: 22 pF
  Crystal: 16 MHz
  Followed the same wiring as the RGB LED supplied by Fritzing, which is not the RGB LED I use
