# Fritzing sketch approxyclock_with_arduino (saved by Fritzing 0.9.6b)
circuit board: 5cm x 10cm
breadboards: 1

parts:
  LED1 = RGB LED (com. cathode, rbg) [package="5 mm [THT]"]
  LED2 = RGB LED (com. cathode, rbg) [package="5 mm [THT]"]
  R1 = Resistor [tolerance=±5% resistance=1k power=0.25 package=THT]
  R2 = Resistor [tolerance=±5% resistance=1k power=0.25 package=THT]
  R3 = Resistor [tolerance=±5% resistance=1k power=0.25 package=THT]
  R4 = Resistor [tolerance=±5% resistance=1k power=0.25 package=THT]
  R5 = Resistor [tolerance=±5% resistance=1k power=0.25 package=THT]
  R6 = Resistor [tolerance=±5% resistance=1k power=0.25 package=THT]
  RHR = Resistor [tolerance=±5% resistance=1k power=0.25 package=THT]
  RHL = Resistor [tolerance=±5% resistance=1k power=0.25 package=THT]
  RSL = Resistor [tolerance=±5% resistance=1M power=0.25 package=THT]
  RTR = Resistor [tolerance=±5% resistance=0 power=0.25 package=THT]
  RTL = Resistor [tolerance=±5% resistance=0 power=0.25 package=THT]
  RSR = Resistor [tolerance=±5% resistance=1M power=0.25 package=THT]
  Part1 = Arduino Uno (Rev3)

nets:
  N1: LED1.red_anode, R1.Pin_1
  N2: LED1.common_cathode, LED2.common_cathode, Part1.GND
  N3: LED1.blue_anode, R2.Pin_1
  N4: LED1.green_anode, R3.Pin_1
  N5: LED2.red_anode, R4.Pin_1
  N6: LED2.blue_anode, R6.Pin_1
  N7: LED2.green_anode, R5.Pin_1
  N8: R1.Pin_0, Part1.D5_PWM
  N9: R2.Pin_0, Part1.D3_PWM
  N10: R3.Pin_0, Part1.D6_PWM
  N11: R4.Pin_0, Part1.D10_PWM/SS
  N12: R5.Pin_0, Part1.D11_PWM/MOSI
  N13: R6.Pin_0, Part1.D9_PWM
  N14: RHR.Pin_0, Part1.D7
  N15: RHR.Pin_1, RTR.Pin_1, RSR.Pin_1
  N16: RHL.Pin_0, RSL.Pin_0, RTL.Pin_1
  N17: RHL.Pin_1, Part1.D2
  N18: RSL.Pin_1, RSR.Pin_0, Part1.D4

notes:
  Followed the same wiring as the RGB LED supplied by Fritzing, which is not the RGB LED I use
